# Fritzing sketch Sketch 3 (saved by Fritzing 0.9.2b)
breadboards: 1

parts:
  Part1 = Arduino Mega 2560 (Rev3)
  Part4 = Arduino MicroSD Shield

nets:
  N1: Part1.AREF, Part4.AREF
  GND: Part1.GND, Part4.GND
  N2: Part1.D9_PWM, Part4.D9
  N3: Part1.IOREF, Part4.5V
  N4: Part1.RESET, Part4.RES
  3V3: Part1.3V3, Part4.3.3V
  N5: Part1.D6_PWM, Part4.D6
  N6: Part1.D7_PWM, Part4.D7
  N7: Part1.D50, Part4.MISO
  N8: Part1.D51, Part4.MOSI
  N9: Part1.D52, Part4.SCK

notes:
  Arduscope
  -A0...A15 imputs
  -USB powered
